# Fritzing sketch project sketchfzz (saved by Fritzing 0.9.3b)
breadboards: 1

parts:
  Part1 = Arduino Micro (Rev3)
  hc-sr1 = hc-sr04  # not connected
  LED1 = smd LED [color="Red (633nm)" package="0603 [SMD]"]
  LED2 = smd LED [color="Red (633nm)" package="0603 [SMD]"]

nets:
  N1: Part1.D9_PWM/A9, LED2.anode
  N2: Part1.D10_PWM/A10, LED1.anode
