# Fritzing sketch arduino_fritzing_sketch (saved by Fritzing 0.9.3b)
breadboards: 1

parts:
  Part1 = Arduino Micro (Rev3)  # not connected
  R1 = Resistor [tolerance=±5% resistance=220 package=THT]
  R2 = Resistor [tolerance=±5% resistance=220 package=THT]
  R3 = Photocell (LDR) [package=THT]
  R4 = Photocell (LDR) [package=THT]
  LED1 = LED - 5mm [color="Blue (430nm)" package="5 mm [THT]"]
  LED3 = LED - 5mm [color="Yellow (592nm)" package="5 mm [THT]"]
  LED2 = smd LED [color="Green (555nm)" package="0603 [SMD]"]

nets:
  N1: R1.Pin_0, R3.pin_1
  N2: R1.Pin_1, R2.Pin_1, LED1.anode, LED3.anode, LED2.anode
  N3: R2.Pin_0, R4.pin_1
  N4: R3.pin_0, R4.pin_0
